# Fritzing sketch PcbSensor_Dev_10-03-2021 (saved by Fritzing 0.9.3b)
circuit board: 15.9522cm x 7.36827cm
breadboards: 1

parts:
  D0 = Rectifier Diode [part_number=1N4001 package="300 mil [THT]"]
  J1 = Camdenboss CTB0158-8 [part_number=CTB0158-8 package=THT]
  J2 = Camdenboss CTB0158-8 [part_number=CTB0158-8 package=THT]
  LED4 = LED - 5mm [color="Red (633nm)" package="5 mm [THT]"]
  LED1 = LED - 5mm [color="Red (633nm)" package="5 mm [THT]"]
  LED2 = LED - 5mm [color="Red (633nm)" package="5 mm [THT]"]
  LED3 = LED - 5mm [color="Red (633nm)" package="5 mm [THT]"]
  ATMEGA-328P = Arduino Nano (Rev3.0)
  1 = FUSE [package=fuse_5mm]
  MAX232N = RS232 Transceiver [package=dil16]
  C1MF = Electrolytic Capacitor [capacitance=1µF package="100 mil [THT, electrolytic]"]
  C1MF_2 = Electrolytic Capacitor [capacitance=1µF package="100 mil [THT, electrolytic]"]
  C1MF_3 = Electrolytic Capacitor [capacitance=1µF package="100 mil [THT, electrolytic]"]
  U3 = MMA_ACCEL_CONNECTOR [package=1x08]
  ULN2803APG = Darlington Driver [package=dil18]
  U5 = MMA_ACCEL_CONNECTOR [package=1x08]
  R10K = Photocell (LDR) [package=THT]
  C1MF_4 = Electrolytic Capacitor [capacitance=1µF package="100 mil [THT, electrolytic]"]
  DZ3 = Rectifier Diode [part_number=1N4001 package="300 mil [THT]"]
  DZ4 = Rectifier Diode [part_number=1N4001 package="300 mil [THT]"]
  DZ1 = Rectifier Diode [part_number=1N4001 package="300 mil [THT]"]
  DZ2 = Rectifier Diode [part_number=1N4001 package="300 mil [THT]"]
  R10K_2 = Photocell (LDR) [package=THT]
  R10K_3 = Photocell (LDR) [package=THT]
  R10K_4 = Photocell (LDR) [package=THT]
  R10K_5 = Photocell (LDR) [package=THT]
  R10K_6 = Photocell (LDR) [package=THT]
  C_4MF = Ceramic Capacitor [capacitance=100nF package="200 mil [THT, multilayer]"]
  C2200MF = Electrolytic Capacitor [capacitance=100µF package="200 mil [THT, electrolytic]"]
  C_4MF_2 = Ceramic Capacitor [capacitance=100nF package="200 mil [THT, multilayer]"]
  D1 = Rectifier Diode [part_number=1N4001 package="300 mil [THT]"]
  D2 = Rectifier Diode [part_number=1N4001 package="300 mil [THT]"]
  D4 = Rectifier Diode [part_number=1N4001 package="300 mil [THT]"]
  RELAY_4 = OMRON PCB Power Relay – G5LE [part_number="G5LE-1\n" package=THT]
  RELAY_3 = OMRON PCB Power Relay – G5LE [part_number="G5LE-1\n" package=THT]
  RELAY_2 = OMRON PCB Power Relay – G5LE [part_number="G5LE-1\n" package=THT]
  RELAY_1 = OMRON PCB Power Relay – G5LE [part_number="G5LE-1\n" package=THT]
  DIP_SWITCH_8_CH = DIP Switch 8 Position [package=dipswitch-08]
  C1MF_5 = Electrolytic Capacitor [capacitance=1µF package="100 mil [THT, electrolytic]"]
  C2200MF_2 = Electrolytic Capacitor [capacitance=100µF package="200 mil [THT, electrolytic]"]
  REG_5V = Voltage Regulator - 5V [package="TO220 [THT]"]
  1_2 = Photocell (LDR) [package=THT]
  1_3 = Photocell (LDR) [package=THT]
  1_4 = Photocell (LDR) [package=THT]
  1_5 = Photocell (LDR) [package=THT]
  1_6 = Photocell (LDR) [package=THT]
  1_7 = Photocell (LDR) [package=THT]
  1_8 = Photocell (LDR) [package=THT]
  1_9 = Photocell (LDR) [package=THT]
  1_10 = Photocell (LDR) [package=THT]
  1_11 = Photocell (LDR) [package=THT]
  1_12 = Photocell (LDR) [package=THT]
  1_13 = Photocell (LDR) [package=THT]
  1_14 = Photocell (LDR) [package=THT]
  1_15 = Photocell (LDR) [package=THT]
  1_16 = Photocell (LDR) [package=THT]
  D3 = Rectifier Diode [part_number=1N4001 package="300 mil [THT]"]
  R1K = Photocell (LDR) [package=THT]
  R1K_2 = Photocell (LDR) [package=THT]
  R1K_3 = Photocell (LDR) [package=THT]
  R1K_4 = Photocell (LDR) [package=THT]
  PC817 = Sharp PC817 [package=THT]
  PC817_2 = Sharp PC817 [package=THT]
  PC817_3 = Sharp PC817 [package=THT]
  PC817_4 = Sharp PC817 [package=THT]
  PC817_5 = Sharp PC817 [package=THT]
  PC817_6 = Sharp PC817 [package=THT]
  PC817_7 = Sharp PC817 [package=THT]
  PC817_8 = Sharp PC817 [package=THT]
  A9G = A9G-Pudding [part_number=A9G-Pudding]
  REG_5V_2 = Voltage Regulator - 5V [package="TO220 [THT]"]
  RS = TRANSISTOR_NPN [package=sot23]
  R1K_5 = Resistor [tolerance=±5% resistance=220 package="0805 [SMD]"]
  REG_5V_3 = Voltage Regulator - 5V [package="TO220 [THT]"]
  NFC_IC2 = KA78R05 Low Dropout Voltage Regulator [part_number=KA78R05 package=TO-220F-4L]
  TMP_1 = KA78R05 Low Dropout Voltage Regulator [part_number=KA78R05 package=TO-220F-4L]
  TMP_2 = KA78R05 Low Dropout Voltage Regulator [part_number=KA78R05 package=TO-220F-4L]
  RK1 = Resistor [tolerance=±5% resistance=220 package="0805 [SMD]"]
  RS1 = TRANSISTOR_NPN [package=sot23]
  ESP32 = ESP32S-HiLetgo [part_number=ESP32S-HiLetgo]
  R5K = Photocell (LDR) [package=THT]
  1_17 = Photocell (LDR) [package=THT]
  OLED_SP32 = KA78R05 Low Dropout Voltage Regulator [part_number=KA78R05 package=TO-220F-4L]
  TMP_3 = KA78R05 Low Dropout Voltage Regulator [part_number=KA78R05 package=TO-220F-4L]
  LM393 = LM393 [package=so08]
  R5K_2 = Resistor [tolerance=±5% resistance=220 package="0805 [SMD]"]
  R5K_3 = Resistor [tolerance=±5% resistance=220 package="0805 [SMD]"]
  R5K_4 = Resistor [tolerance=±5% resistance=220 package="0805 [SMD]"]
  R5k = Resistor [tolerance=±5% resistance=220 package="0805 [SMD]"]
  R5K_5 = Resistor [tolerance=±5% resistance=220 package="0805 [SMD]"]
  R5K_6 = Resistor [tolerance=±5% resistance=220 package="0805 [SMD]"]

nets:
  N1: D0.cathode, C_4MF.0, C2200MF.+, REG_5V.input_voltage, REG_5V_2.input_voltage, REG_5V_3.input_voltage
  N2: D0.anode, 1.2
  N3: J1.pin1, RELAY_2.A
  N4: J1.pin2, RELAY_3.B
  N5: J1.pin3, RELAY_3.C
  N6: J1.pin4, RELAY_3.A
  N7: J1.pin5, RELAY_4.B
  N8: J1.pin6, RELAY_4.C
  N9: J1.pin7, RELAY_4.A
  N10: J2.pin1, RELAY_1.B
  N11: J2.pin2, RELAY_1.C
  N12: J2.pin3, RELAY_1.A
  N13: J2.pin4, RELAY_2.B
  N14: J2.pin5, RELAY_2.C
  N15: LED4.cathode, ULN2803APG.14, D4.anode, RELAY_4.COIL2
  N16: LED4.anode, R1K_4.pin_1
  N17: LED1.cathode, ULN2803APG.11, D1.anode, RELAY_1.COIL2
  N18: LED1.anode, R1K_2.pin_1
  N19: LED2.cathode, ULN2803APG.12, D2.anode, RELAY_2.COIL2
  N20: LED2.anode, R1K.pin_1
  N21: LED3.cathode, ULN2803APG.13, RELAY_3.COIL2, D3.anode
  N22: LED3.anode, R1K_3.pin_1
  N23: ATMEGA-328P.D1/TX, ESP32.GPIO16
  N24: ATMEGA-328P.D0/RX, ESP32.GPIO17
  N25: ATMEGA-328P.RESET, RS.E
  GND: ATMEGA-328P.GND, MAX232N.GND, ULN2803APG.9, U5.Z, U5.GS1, C1MF_4.-, R10K_2.pin_0, R10K_3.pin_0, R10K_6.pin_0, C_4MF.1, C2200MF.-, C_4MF_2.1, C1MF_5.-, C2200MF_2.-, REG_5V.GND, PC817.Pin_2, PC817_4.Pin_2, PC817_5.Pin_2, PC817_6.Pin_2, PC817_7.Pin_2, PC817_8.Pin_2, A9G.GPIO6, REG_5V_2.GND, RS.C, REG_5V_3.GND, NFC_IC2.VIN, TMP_1.VIN, TMP_2.VIN, RS1.C, ESP32.GND, OLED_SP32.VIN, TMP_3.VIN, LM393.G1_V-
  N26: ATMEGA-328P.D2, DIP_SWITCH_8_CH.1
  N27: ATMEGA-328P.D3, DIP_SWITCH_8_CH.2
  N28: ATMEGA-328P.D4, DIP_SWITCH_8_CH.3
  N29: ATMEGA-328P.D5, DIP_SWITCH_8_CH.4
  N30: ATMEGA-328P.D6, DIP_SWITCH_8_CH.5
  N31: ATMEGA-328P.D7, DIP_SWITCH_8_CH.6
  N32: ATMEGA-328P.D8, DIP_SWITCH_8_CH.7
  N33: ATMEGA-328P.D9, DIP_SWITCH_8_CH.8
  N34: ATMEGA-328P.D10, DZ1.anode
  N35: ATMEGA-328P.D11/MOSI, MAX232N.T1IN
  N36: ATMEGA-328P.D12/MISO, MAX232N.R1OUT
  VIN: ATMEGA-328P.VIN, MAX232N.VCC, C1MF.+, C1MF_4.+, C_4MF_2.0, D1.cathode, D2.cathode, D4.cathode, RELAY_4.COIL1, RELAY_3.COIL1, RELAY_2.COIL1, RELAY_1.COIL1, C2200MF_2.+, REG_5V.output_voltage, D3.cathode, R1K.pin_0, R1K_2.pin_0, R1K_3.pin_0, R1K_4.pin_0, PC817.Pin_4, PC817_2.Pin_4, PC817_3.Pin_4, PC817_4.Pin_4, PC817_5.Pin_4, PC817_6.Pin_4, PC817_7.Pin_4, PC817_8.Pin_4
  N37: ATMEGA-328P.A5, R10K_2.pin_1, R10K_4.pin_1
  N38: ATMEGA-328P.A4, R10K_3.pin_1, R10K_5.pin_1
  N39: ATMEGA-328P.A3, R10K.pin_1, R10K_6.pin_1
  N40: ATMEGA-328P.A2, DZ4.anode
  N41: ATMEGA-328P.A1, DZ2.anode
  N42: ATMEGA-328P.A0, DZ3.anode
  N43: 1.1, U5.Y
  N44: MAX232N.C1+, C1MF_2.+
  N45: MAX232N.V+, C1MF.-
  N46: MAX232N.C1-, C1MF_2.-
  N47: MAX232N.C2+, C1MF_3.+
  N48: MAX232N.C2-, C1MF_3.-
  N49: MAX232N.V-, C1MF_5.+
  N50: MAX232N.R1IN, U5.GND
  N51: MAX232N.T1OUT, U5.X
  N52: U3.VCC, DZ4.cathode
  N53: U3.GND, DZ3.cathode
  N54: U3.X, DZ2.cathode
  N55: U3.Y, DZ1.cathode
  N56: U3.Z, R10K.pin_0
  N57: U3.GS1, ULN2803APG.16
  N58: U3.GS2, ULN2803APG.17
  N59: U3.SLP, ULN2803APG.18
  N60: ULN2803APG.1, 1_2.pin_1
  N61: ULN2803APG.2, 1_6.pin_1
  N62: ULN2803APG.3, 1_7.pin_1
  N63: ULN2803APG.4, 1_8.pin_1
  N64: ULN2803APG.5, 1_9.pin_1
  N65: ULN2803APG.6, 1_5.pin_1
  N66: ULN2803APG.7, 1_4.pin_1
  N67: ULN2803APG.8, 1_3.pin_1
  N68: ULN2803APG.15, U5.VCC
  N69: U5.GS2, R10K_4.pin_0
  N70: U5.SLP, R10K_5.pin_0
  N71: DIP_SWITCH_8_CH.9, 1_15.pin_0
  N72: DIP_SWITCH_8_CH.10, 1_14.pin_0
  N73: DIP_SWITCH_8_CH.11, 1_13.pin_0
  N74: DIP_SWITCH_8_CH.12, 1_16.pin_0
  N75: DIP_SWITCH_8_CH.13, 1_12.pin_0
  N76: DIP_SWITCH_8_CH.14, 1_11.pin_0
  N77: DIP_SWITCH_8_CH.15, 1_10.pin_0
  N78: DIP_SWITCH_8_CH.16, 1_17.pin_0
  N79: 1_2.pin_0, PC817.Pin_3
  N80: 1_3.pin_0, PC817_5.Pin_3
  N81: 1_4.pin_0, PC817_6.Pin_3
  N82: 1_5.pin_0, PC817_4.Pin_3
  N83: 1_6.pin_0, PC817_2.Pin_3
  N84: 1_7.pin_0, PC817_8.Pin_3
  N85: 1_8.pin_0, PC817_3.Pin_3
  N86: 1_9.pin_0, PC817_7.Pin_3
  N87: 1_10.pin_1, PC817_2.Pin_1
  N88: 1_11.pin_1, PC817_8.Pin_1
  N89: 1_12.pin_1, PC817_3.Pin_1
  N90: 1_13.pin_1, PC817_5.Pin_1
  N91: 1_14.pin_1, PC817_6.Pin_1
  N92: 1_15.pin_1, PC817_4.Pin_1
  N93: 1_16.pin_1, PC817_7.Pin_1
  N94: PC817.Pin_1, 1_17.pin_1
  N95: PC817_2.Pin_2, PC817_3.Pin_2
  N96: A9G.GPIO25, ESP32.GPIO21
  N97: A9G.GPIO26, ESP32.GPIO22
  N98: A9G.GPIO27, ESP32.GPIO33
  N99: A9G.GPIO14, ESP32.GPIO27
  N100: A9G.GPIO12, ESP32.GPIO13
  N101: A9G.GND, ESP32.GPIO12
  N102: A9G.GPIO13, ESP32.GPIO14
  N103: A9G.GPIO7, REG_5V_3.output_voltage
  N104: A9G.GPIO8, RS1.E
  N105: A9G.GPIO3, ESP32.GPIO5
  N106: A9G.GPIO1, ESP32.GPIO18
  N107: REG_5V_2.output_voltage, ESP32.VIN, OLED_SP32.VOUT
  N108: RS.B, R1K_5.Pin_1
  N109: R1K_5.Pin_0, ESP32.GPIO39
  N110: NFC_IC2.VOUT, TMP_1.VOUT, TMP_2.VOUT, ESP32.3.3, R5K.pin_0, TMP_3.VOUT, LM393.G1_+IN, LM393.G2_+IN, LM393.G1_V+, R5K_2.Pin_1, R5K_3.Pin_1, R5K_4.Pin_1, R5k.Pin_0, R5K_5.Pin_0, R5K_6.Pin_1
  GND_2: NFC_IC2.GND, ESP32.GPIO19, OLED_SP32.GND, R5K_5.Pin_1
  N111: NFC_IC2.EN, ESP32.GPIO23, OLED_SP32.EN, R5K_6.Pin_0
  N112: TMP_1.GND, LM393.G2_-IN, R5K_4.Pin_0
  N113: TMP_1.EN, TMP_2.EN, ESP32.GPIO4, R5K.pin_1, TMP_3.EN
  N114: TMP_2.GND, LM393.G1_-IN, R5K_3.Pin_0
  N115: RK1.Pin_0, ESP32.GPIO36
  N116: RK1.Pin_1, RS1.B
  N117: ESP32.GPIO34, LM393.G1_OUT, R5K_2.Pin_0
  N118: ESP32.GPIO32, LM393.G2_OUT, R5k.Pin_1

notes:
  R220
  R1K
  |||
  TERMINAL_RELAY
  1234
  BOARD_SENSOR_ERB_VER_1.0
  FJLIC_VER_1.0
  FJ_LOW_INTEGRATE_COST
  COM
  N_C
  N_O
  __
  FJLIC IOT GPRS/GPS + WIFI
  ***
  ____
  FUS_3AMP
  FJ_LOW_INTEGRATE_COST / MODEL ERB THROUGH-HOLE DEV
  ERB_BOARD_IOT
  A9G-PUDDING
  GPRS/GPS+SD
  Author:
  Javier Flores Z
  Contact:
  soporte@fjlic.com
  Url:
  fjlic.com
  ERB--IOT
  GitHub:
  fjlic/IOT-Hotspot

custom parts:
  Camdenboss CTB0158-8: Camdenboss CTB0158-8 5.08mm (0.2") Pitch Standard Profile 90 ̊ Rising Clamp Terminal, 8 pole The real-life connectors are modular, made up of two or three connector blocks slotted together. These can be further slotted together to make larger connectors. Fritzing part is derived from Screw terminals by Lionel Michel. Because of the offset between connection pins and screw terminals, these are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
  A9G-Pudding: A9G-Pudding Development Board GPRSi + GPS + SD Dual Cores Microcontroller and management modules, and the entire solution occupies the least area of PCB performance is the best, safe and reliable, easy to extend to a variety of applications
  ESP32S-HiLetgo: HiLetgo ESP-WROOM-32 ESP32 ESP-32S Development Board 2.4GHz Dual-Mode WiFi + Bluetooth Dual Cores Microcontroller The ESP32 integrated with Antenna switches, RF Balun, power amplifiers, low-noise amplifiers, filters, and management modules, and the entire solution occupies the least area of PCB. 2.4 GHz Wi-Fi plus Bluetooth dual-mode chip, with TSMC Ultra-low power consumption 40nm technology,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
